# Fritzing sketch 1 (saved by Fritzing 0.9.2b)
breadboards: 1

parts:
  part = Arduino Due (Rev2b)
  Raspberry_Pi1 = Raspberry Pi 2
  Reverse_Switch = SWITCH-MOMENTARY-2 [package=tactile_switch_smd-2]
  Left_Turn_Signal = SWITCH-MOMENTARY-2 [package=tactile_switch_smd-2]
  Right_Turn_Signal = SWITCH-MOMENTARY-2 [package=tactile_switch_smd-2]
  Left_Turn_Switch = SWITCH-MOMENTARY-2 [package=tactile_switch_smd-2]
  Right_Turn_Switch = SWITCH-MOMENTARY-2 [package=tactile_switch_smd-2]
  Reverse_Switch5 = SWITCH-MOMENTARY-2 [package=tactile_switch_smd-2]
  Reverse_Switch6 = SWITCH-MOMENTARY-2 [package=tactile_switch_smd-2]
  Reverse_Switch7 = SWITCH-MOMENTARY-2 [package=tactile_switch_smd-2]

nets:
  N1: part.SDA1, Raspberry_Pi1.GPIO2
  N2: part.SCL1, Raspberry_Pi1.GPIO3
  N3: part.D22, Reverse_Switch.1
  N4: part.D23, Left_Turn_Signal.1
  N5: part.D24, Right_Turn_Signal.1
  N6: part.D25, Left_Turn_Switch.1
  N7: part.D26, Right_Turn_Switch.1
  N8: part.D27, Reverse_Switch5.1
  N9: part.D28, Reverse_Switch6.1
  N10: part.D29, Reverse_Switch7.1
